# Fritzing sketch 500C 1000C Compact Power Dev Board (saved by Fritzing 0.9.8b)
circuit board: 4.74814cm x 3.64147cm
breadboards: 1

parts:
  1000C = Adafruit PowerBoost 1000C [part_number="Adafruit #2465"]
  BATTERY = Header 2 [package=jst-2-pth-ns]
  OUTPUT = female pin header, 3 pins [form="♀ (female)"]
  500C = female pin header, 8 pins [form="♀ (female)"]
  BAT_MONITOR = Header 2 [package=jst-2-pth-ns]
  5V_IN = female pin header, 2 pins [form="♀ (female)"]
  5V_OUT = female pin header, 2 pins [form="♀ (female)"]

nets:
  GND: 1000C.GND, BATTERY.1, OUTPUT.pin2, 500C.pin2, 500C.pin5, 500C.pin7, BAT_MONITOR.1, 5V_IN.pin2, 5V_OUT.pin1
  N1: 1000C.5.0V, 500C.pin8, 5V_OUT.pin2
  N2: 1000C.VBUS, 500C.pin1, 5V_IN.pin1
  N3: 1000C.VLIPO, BATTERY.2, 500C.pin3, BAT_MONITOR.2
  N4: 1000C.ENABLE, OUTPUT.pin1, 500C.pin4

notes:
  ENABLE
  GND
  +5
  USB IN
  BAT
  VS
  LBO
  NC
  5V
  + -
  POWERBOOST 500C / 1000C
  ON
  OFF
  github.com/GOTO-GOSUB

custom parts:
  Adafruit PowerBoost 1000C: PowerBoost 1000C is the perfect power supply for your portable project! With a built-in load-sharing battery charger circuit, you'll be able to keep your power-hungry project running even while recharging the battery! This little DC/DC boost converter module can be powered by any 3.7V LiIon/LiPoly battery, and convert the battery output to 5.2V DC for running your 5V projects.
